// Logisim project 1801042692.circ as structural Verilog
module lab1 (
  input  A,
  input  B,
  input  C,
  input  D,
  output out_5
);

  wire and_1_out, and_2_out, and_3_out, and_4_out, and_5_out, and_6_out, and_7_out, and_8_out, not_1_out,
       not_2_out, not_3_out;

  not not_1 (not_1_out, A);
  not not_2 (not_2_out, B);
  not not_3 (not_3_out, A);
  not not_4 (not_3_out, B);
  and and_1 (and_1_out, not_1_out, not_2_out, not_3_out, B);
  and and_2 (and_2_out, not_1_out, not_2_out, A, B);
  and and_3 (and_3_out, not_1_out, B, not_3_out, B);
  and and_4 (and_4_out, not_1_out, B, A, not_3_out);
  and and_5 (and_5_out, A, not_2_out, not_3_out, B);
  and and_6 (and_6_out, A, not_2_out, A, not_3_out);
  and and_7 (and_7_out, A, B, not_3_out, not_3_out);
  and and_8 (and_8_out, A, B, A, B);
  or or_1 (out_5, and_1_out, and_2_out, and_3_out, and_4_out, and_5_out, and_6_out, and_7_out, and_8_out);

  assign C = A;
  assign D = B;
endmodule
