// Logisim project lab3.circ as structural Verilog: 1 circuit, main circuit main
module main (
  input  A,
  input  B,
  input  C,
  input  D,
  input  E,
  output out_6
);

  wire and_1_out, and_2_out, and_3_out, and_4_out, not_1_out, not_2_out, not_3_out, not_4_out, not_5_out,
       not_6_out;

  not not_1 (not_1_out, A);
  not not_2 (not_2_out, B);
  not not_3 (not_3_out, B);
  not not_4 (not_4_out, E);
  not not_5 (not_5_out, C);
  not not_6 (not_6_out, D);
  and and_1 (and_1_out, not_1_out, not_3_out, C, E);
  and and_2 (and_2_out, not_2_out, C, D, E);
  and and_3 (and_3_out, not_1_out, B, C, D, not_4_out);
  and and_4 (and_4_out, A, B, not_5_out, not_6_out, E);
  or or_1 (out_6, and_1_out, and_2_out, and_3_out, and_4_out);
endmodule
